# Fritzing sketch remoht-arduino (saved by Fritzing 0.7.11b)

parts:
  Arduino = Arduino Pro Mini 3.3V
  T1 = LM35 Temperature Sensor [package="TO92 [THT]"]
  LDR = Photocell (LDR) [package=THT]
  Relay_2 = LED - 5mm [color="Red (633nm)" package="5 mm [THT]"]
  Relay_1 = LED - 5mm [color="Red (633nm)" package="5 mm [THT]"]
  PIR = Infrared Proximity Sensor
  Power = Power plug
  R1 = 1k Ω Resistor [package=THT]

nets:
  VCC: Arduino.VCC, T1.+Vs, LDR.pin_1, PIR.Vcc, Power.VCC
  GND: Arduino.GND, T1.GND, Power.GND, R1.Pin_1
  N1: Arduino.A1, T1.Vout
  N2: Arduino.A0, LDR.pin_0, R1.Pin_0
  N3: Arduino.D4, PIR.Vout
  N4: Arduino.D3, Relay_1.anode
  N5: Arduino.D2, Relay_2.anode
  N6: Relay_2.cathode, Relay_1.cathode, PIR.GND
